# Fritzing sketch ECU-Bombyx (saved by Fritzing 0.9.4)
circuit board: 8.46667cm x 5.64444cm
breadboards: 1

parts:
  ZS-042_RTC1 = ZS-042 RTC Module
  microSD1 = MicroSD Card Module
  Componente2 = Arduino Uno (Rev3)
  DHT1 = DHT22 module

nets:
  GND: ZS-042_RTC1.GND, microSD1.GND, Componente2.GND, DHT1.GND
  VCC: ZS-042_RTC1.VCC, microSD1.VCC, Componente2.5V, DHT1.VCC
  N1: ZS-042_RTC1.SDA, Componente2.A4/SDA
  N2: ZS-042_RTC1.SCL, Componente2.A5/SCL
  N3: microSD1.MISO, Componente2.D12/MISO
  N4: microSD1.MOSI, Componente2.D11_PWM/MOSI
  N5: microSD1.SCK, Componente2.D13/SCK
  N6: microSD1.CS, Componente2.D8
  N7: Componente2.D2, DHT1.DAT

custom parts:
  DHT22 module: Digital relative humidity & temperature sensor DHT22 module
